# Fritzing sketch circuit (saved by Fritzing 0.9.3b)
breadboards: 1

parts:
  TFT1 = 1.44" SPI TFT Graphics Display 128x128 [package=THT]
  Part1 = Triple Axis Accelerometer Breakout - ADXL345
  Part2 = Arduino Uno (Rev3) - ICSP

nets:
  VCC: TFT1.VCC, Part1.VCC, Part2.3V3
  GND: TFT1.GND, Part1.GND, Part2.GND
  N1: TFT1.CS, Part2.D10_PWM/SS
  N2: TFT1.RESET, Part2.D8
  N3: TFT1.A0, Part2.D9_PWM
  N4: TFT1.SDA, Part2.D11_PWM/MOSI
  N5: TFT1.SCK, Part2.D13/SCK
  N6: TFT1.LED, Part2.5V
  N7: Part1.SDA, Part2.A4/SDA
  N8: Part1.SCL, Part2.A5/SCL

custom parts:
  1.44" SPI TFT Graphics Display 128x128: This is for https://www.amazon.com/gp/product/B07B4BDWCL/ref=ask_ql_qh_dp_hza display. Note that this display is sold with a misprinted silkscreen indicating I2C connections on P2 connector, it is actualy SPI. The P1 connections are non functional on this board from the linked URL seller on Amazon.
